# Fritzing sketch 8ball (saved by Fritzing 0.9.3b)

parts:
  GY1 = MPU-6050 Board GY-521 [form="♀ (female)" package=THT]
  Part1 = Arduino Uno (Rev3)
  Squix1 = OLED 0.96" 128x64 I2C SSD1306

nets:
  N1: GY1.pin1, Part1.3V3
  GND: GY1.pin2, Part1.GND, Squix1.GND
  N2: GY1.pin3, Part1.A5/SCL, Squix1.SCL
  N3: GY1.pin4, Part1.A4/SDA, Squix1.SCA
  N4: GY1.pin8, Part1.D2
  5V: Part1.5V, Squix1.VCC

custom parts:
  MPU-6050 Board GY-521: Acelerometro y Giroscopio MPU-6050 Board GY-521
